// Logisim project pacemakerlogic.circ as structural Verilog: 1 circuit, main circuit main
module main (
  input  DIGITAL_HERTBEAT_PULSE,
  input  Power_on_resets_at_heartbeat_pulse,
  input  HEARTBEAT_PULSE_WITH_GENERATED,
  output PULSE_GENERATOR_SIGNAL
);

  wire and_2_out, and_3_out, and_4_out, and_5_out, and_6_out, CLK_50ms_out, j_k_ff_1_q, j_k_ff_2_q,
       j_k_ff_3_q, j_k_ff_4_q, nor_1_out, nor_2_out, nor_3_out, nor_4_out, nor_6_out, not_1_out, not_2_out,
       not_3_out, not_4_out, not_5_out, not_6_out, not_7_out, or_1_out, or_2_out, or_3_out, OSC_CLR,
       Oscillator, xnor_1_out, xnor_2_out;

  or or_1 (or_1_out, Power_on_resets_at_heartbeat_pulse, nor_3_out);
  Clock CLK_50ms (.out(CLK_50ms_out));
  not not_1 (not_1_out, or_3_out);
  and and_1 (OSC_CLR, DIGITAL_HERTBEAT_PULSE, or_1_out);
  not not_2 (not_2_out, CLK_50ms_out);
  not not_3 (not_3_out, not_1_out);
  not not_4 (not_4_out, not_3_out);
  not not_5 (not_5_out, OSC_CLR);
  not not_6 (not_6_out, OSC_CLR);
  and and_2 (and_2_out, not_3_out, not_2_out);
  and and_3 (and_3_out, not_2_out, not_4_out);
  J_K_Flip_Flop j_k_ff_1 (
    .J(OSC_CLR), .K(OSC_CLR), .clk(Oscillator), .Q(j_k_ff_1_q), .reset(OSC_CLR));  // open: Qn, preset
  not not_7 (not_7_out, not_5_out);
  and and_4 (and_4_out, not_6_out, j_k_ff_2_q);
  nor nor_1 (nor_1_out, and_2_out, or_2_out);
  nor nor_2 (nor_2_out, nor_1_out, and_3_out);
  or or_2 (or_2_out, nor_2_out, OSC_CLR);
  J_K_Flip_Flop j_k_ff_2 (
    .J(OSC_CLR), .K(OSC_CLR), .clk(Oscillator), .Q(j_k_ff_2_q), .reset(OSC_CLR));  // open: Qn, preset
  nor nor_3 (nor_3_out, not_7_out, nor_4_out);
  nor nor_4 (nor_4_out, nor_3_out, and_4_out);
  and and_5 (and_5_out, nor_1_out, CLK_50ms_out);
  and and_6 (and_6_out, CLK_50ms_out, or_2_out);
  J_K_Flip_Flop j_k_ff_3 (
    .J(HEARTBEAT_PULSE_WITH_GENERATED), .K(HEARTBEAT_PULSE_WITH_GENERATED), .clk(Oscillator), .Q(j_k_ff_3_q),
    .reset(HEARTBEAT_PULSE_WITH_GENERATED));  // open: Qn, preset
  nor nor_5 (Oscillator, and_5_out, or_3_out);
  nor nor_6 (nor_6_out, Oscillator, and_6_out);
  or or_3 (or_3_out, nor_6_out, OSC_CLR);
  J_K_Flip_Flop j_k_ff_4 (
    .J(HEARTBEAT_PULSE_WITH_GENERATED), .K(HEARTBEAT_PULSE_WITH_GENERATED), .clk(Oscillator), .Q(j_k_ff_4_q),
    .reset(HEARTBEAT_PULSE_WITH_GENERATED));  // open: Qn, preset
  xnor xnor_1 (xnor_1_out, j_k_ff_1_q, j_k_ff_3_q);
  xnor xnor_2 (xnor_2_out, j_k_ff_2_q, j_k_ff_4_q);
  and and_7 (PULSE_GENERATOR_SIGNAL, xnor_1_out, xnor_2_out);

  // Notes on the sheet:
  //   Then use a comprator to get digital output
  //   Number of pulses experience by cardiac muscles
  //   Use a transistor pair to amplify the heartbeat pulse
  //   This Pulse must last till first heartbeat, use a flip flop to sustain after powerup
endmodule
